# Fritzing sketch slam_bot (saved by Fritzing 0.9.9b)

parts:
  M1 = RPlidar A1M8 [package=THT]  # not connected
  Part1 = Arduino Mega 2560 (Rev3)
  M2 = BTS7960
  M3 = BTS7960
  M4 = RioRand LM2596
  RC_LiPo_Battery1 = RC_LIPO [package=lipo-2200]
  USBTTL1 = USB A Plug
  USBTTL3 = Micro USB B Plug
  Yumo-enc1 = YumoE6B2
  Yumo-enc2 = YumoE6B2
  M7 = Planetary Gearmotor  # not connected
  M8 = Planetary Gearmotor  # not connected
  FTDI_USB_UART1 = RPLiDAR USB [part_number="USB UART"]  # not connected
  USBTTL4 = USB A Plug
  USBTTL5 = Micro USB B Plug

nets:
  N1: Part1.D19/RX1, Yumo-enc1.A
  N2: Part1.D18/TX1, Yumo-enc1.B
  N3: Part1.D11_PWM, M2.pin4
  N4: Part1.D10_PWM, M2.pin3
  N5: Part1.D9_PWM, M3.pin4
  N6: Part1.D8_PWM, M3.pin3
  GND: Part1.GND, M2.pin8, M3.pin8, M4.Pin_4, Yumo-enc1.GND, Yumo-enc2.GND
  N7: Part1.D2_PWM, Yumo-enc2.A
  N8: Part1.D3_PWM, Yumo-enc2.B
  N9: Part1.D4_PWM, M3.pin1
  N10: Part1.D5_PWM, M3.pin2
  N11: Part1.D6_PWM, M2.pin1
  N12: Part1.D7_PWM, M2.pin2
  N13: Part1.5V, M2.pin7, M3.pin7
  N14: M2.pin11, M3.pin11, M4.Pin_1, RC_LiPo_Battery1.+
  N15: M2.pin12, M3.pin12, M4.Pin_2, RC_LiPo_Battery1.-
  N16: M4.Pin_3, Yumo-enc2.V
  N17: USBTTL1.usb, USBTTL3.usb
  N18: USBTTL4.usb, USBTTL5.usb

notes:
  RIGHT MOTOR
  LEFT MOTOR
  RIGHT ENCODER
  LEFT ENCODER

custom parts:
  RPlidar A1M8: .The RPLIDAR A1 is the next generation low cost 360 degree 2D laser scanner (LIDAR) solution developed by SLAMTEC. It can take up to 4000 samples of laser ranging per second with high rotation speed. And equipped with SLAMTEC patented OPTMAG technology, it breakouts the life limitation of traditional LIDAR system so as to work stably for a long time.
  BTS7960: BTS7960 43A Peak Power H-Bridge PWM Motor Driver
  RC_LIPO: RC LiPo Battery
  USB A Plug: USB A Plug breadboard only for documetnation purposes.
  YumoE6B2: Yumo E6B2-C incremental encoder. Resolutions 10 to 4000 pulses per revolution (depending on model number). Power from 5 to 24V (again depending on model). Dia 40mm body 30mm plus 20mm shaft.
  Planetary Gearmotor: Your standard DC Motor
  RPLiDAR USB: CP2102 USB UART FTDI
